# Fritzing sketch Fritzing Sketch Source File (3 Pin) (saved by Fritzing 0.9.3b)
breadboards: 1

parts:
  U1 = NodeMCU V3.0
  DHT1 = DHT11 Humitidy and Temperature Sensor (3 pins)
  R1 = Resistor [tolerance=±5% resistance=10k package="0402 [SMD]"]

nets:
  N1: U1.D2, DHT1.DATA
  N2: U1.3V3, R1.Pin_1
  N3: U1.GND#6, U1.GND#13, U1.GND#16, U1.GND#33
  N4: U1.GND#41, DHT1.GND
  N5: DHT1.VDD, R1.Pin_0

notes:
  GND - Black
  VCC - Red
  GPIO - Blue
  DHT11 / DHT22 Sensor
  (3 Pins)
  With Flutter App
  www.webdevfusion.com

custom parts:
  NodeMCU V3.0: ESP8266 based NodeMCU
  DHT11 Humitidy and Temperature Sensor (3 pins): DHT11 Humidity and Temperature Sensor (3 pins) from the design created by John De Cristofaro for Adafruit Industries.
