# Fritzing sketch Fritzing Sketch Source File (4 Pin) (saved by Fritzing 0.9.3b)
breadboards: 1

parts:
  U1 = NodeMCU V3.0
  R1 = Resistor [tolerance=±5% resistance=10k package="0402 [SMD]"]
  DHT2 = DHT11 Humitidy and Temperature Sensor

nets:
  N1: U1.D2, DHT2.DATA
  N2: U1.3V3, R1.Pin_1
  N3: U1.GND#6, U1.GND#13, U1.GND#16, U1.GND#33
  N4: U1.GND#41, DHT2.GND
  N5: R1.Pin_0, DHT2.VDD

notes:
  GND - Black
  VCC - Red
  GPIO - Blue
  DHT11 / DHT22 Sensor
  (4 Pins)
  With Flutter App
  www.webdevfusion.com

custom parts:
  NodeMCU V3.0: ESP8266 based NodeMCU
  DHT11 Humitidy and Temperature Sensor: DHT11 Humidity and Temperature Sensor
